// Logisim project COA_final_project_1.circ as structural Verilog: 19 circuits, main circuit main
module main (
  input  B,
  input  A,
  input  carry_in,
  input  [1:0] Operator,
  input  in_5,
  output out1,
  output carry_out
);

  wire adder_1_out, and_gate_out, multiplexer_1_out, not_1_out, or_gate_out;

  not not_1 (not_1_out, B);
  Multiplexer #(.disabled("Z")) multiplexer_1 (.in0(B), .in1(not_1_out), .out(multiplexer_1_out), .sel(in_5));
  and and_gate (and_gate_out, A, multiplexer_1_out);
  or or_gate (or_gate_out, A, multiplexer_1_out);
  Adder #(.width(1)) adder_1 (.a(A), .b(multiplexer_1_out), .out(adder_1_out), .cin(carry_in), .cout(carry_out));
  Multiplexer #(.select(2)) multiplexer_2 (
    .in0(and_gate_out), .in1(or_gate_out), .in2(adder_1_out), .out(out1), .sel(Operator));  // open: in3

  // Notes on the sheet:
  //   Adder
endmodule

module register16bit_LSBMSB (
  input  [15:0] Data,
  input  WE,
  input  Clk,
  input  Reset,
  input  OE,
  output [15:0] Result,
  output [15:0] Dout,
  output [7:0] Eight_LSBs,
  output [7:0] Eight_MSBs
);

  Register #(.width(16)) register_1 (.D(Data), .en(WE), .clk(Clk), .Q(Result), .clr(Reset));
  assign Dout = OE ? Result : 16'bz;  // Controlled_Buffer controlled_buffer_1
  BitSelector #(.group(8), .width(16)) bitselector_1 (.in(Dout), .out(Eight_MSBs), .sel(1'b1));
  BitSelector #(.group(8), .width(16)) bitselector_2 (.in(Dout), .out(Eight_LSBs), .sel(1'b0));
endmodule

module register16bits (
  input  [15:0] Data,
  input  WE,
  input  Clk,
  input  Reset,
  output [15:0] Result
);

  Register #(.width(16)) register_1 (.D(Data), .en(WE), .clk(Clk), .Q(Result), .clr(Reset));
endmodule

module datapath (
  input  [15:0] Data_in,
  input  OE,
  input  IR_OE,
  input  MBR_OE,
  input  in_5,
  input  [3:0] AUsel,
  input  MBR_WE,
  input  [2:0] RUsel,
  input  OutReg_WE,
  input  OutReg_OE,
  output [15:0] out_11
);

  wire clock_1_out, clock_2_out;
  wire [7:0] bitselector_1_out, MAR_result;
  wire [15:0] controlled_buffer_1_out, Instruction_Register_result, MBR_result, project_alu_1_p2,
       project_alu_1_p5, Register_A_result;

  Clock clock_1 (.out(clock_1_out));
  BitSelector #(.group(8), .width(16)) bitselector_1 (
    .in(controlled_buffer_1_out), .out(bitselector_1_out), .sel(1'b1));
  assign controlled_buffer_1_out = IR_OE ? Instruction_Register_result : 16'bz;  // Controlled_Buffer controlled_buffer_1
  register16bits Instruction_Register (
    .Data(project_alu_1_p5), .Clk(clock_1_out), .Result(Instruction_Register_result));  // open: WE, Reset
  register16bits Register_A (
    .Data(project_alu_1_p5), .Clk(clock_1_out), .Result(Register_A_result));  // open: WE, Reset
  // project_alu project_alu_1: pin names not known; wires that end beside it: Register_A_result, project_alu_1_p2, AUsel, RUsel, project_alu_1_p5
  register16bits Register_B (.Data(project_alu_1_p5), .Clk(clock_1_out), .Result(project_alu_1_p2));  // open: WE, Reset
  assign project_alu_1_p5 = OE ? Data_in : 16'bz;  // Controlled_Buffer controlled_buffer_2
  assign project_alu_1_p5 = MBR_OE ? MBR_result : 16'bz;  // Controlled_Buffer controlled_buffer_3
  register8bit MAR (.Data(bitselector_1_out), .Clk(clock_2_out), .Result(MAR_result));  // open: WE, Reset
  register16bits MBR (.WE(MBR_WE), .Data(project_alu_1_p5), .Clk(clock_2_out), .Result(MBR_result));  // open: Reset
  register16bits Output_Register (
    .WE(OutReg_WE), .Data(project_alu_1_p5), .Clk(clock_2_out), .Result(out_11));  // open: Reset
  assign project_alu_1_p5 = OutReg_OE ? out_11 : 16'bz;  // Controlled_Buffer controlled_buffer_4
  Clock clock_2 (.out(clock_2_out));
  assign project_alu_1_p5 = in_5 ? MBR_result : 16'bz;  // Controlled_Buffer controlled_buffer_5

  // Notes on the sheet:
  //   Datapath
endmodule

module project_ao (
  input  [3:0] AUsel,
  input  [15:0] A,
  input  [15:0] B,
  output [15:0] Auresult
);

  wire [15:0] adder_1_out, and_1_out, divider_1_out, multiplier_1_out, negator_1_out, negator_2_out,
       or_1_out, shifter_1_out, shifter_2_out, shifter_3_out, shifter_4_out, subtractor_1_out, xor_1_out;

  Adder #(.width(16)) adder_1 (.a(A), .b(B), .out(adder_1_out));  // open: cin, cout
  Divider #(.width(16)) divider_1 (.a(A), .b(B), .out(divider_1_out));  // open: upper, rem
  Multiplier #(.width(16)) multiplier_1 (.a(A), .b(B), .out(multiplier_1_out));  // open: cin, cout
  Subtractor #(.width(16)) subtractor_1 (.a(A), .b(B), .out(subtractor_1_out));  // open: bin, bout
  Shifter #(.width(16)) shifter_1 (.in(A), .\dist (4'b0010), .out(shifter_1_out));
  Shifter #(.width(16)) shifter_2 (.in(B), .\dist (4'b0010), .out(shifter_2_out));
  Shifter #(.shift("lr"), .width(16)) shifter_3 (.in(A), .\dist (4'b0010), .out(shifter_3_out));
  Shifter #(.shift("lr"), .width(16)) shifter_4 (.in(B), .\dist (4'b0010), .out(shifter_4_out));
  Negator #(.width(16)) negator_1 (.in(A), .out(negator_1_out));
  Negator #(.width(16)) negator_2 (.in(B), .out(negator_2_out));
  assign and_1_out = A & B;  // AND_Gate and_1, 16 bits wide
  assign or_1_out = A | B;  // OR_Gate or_1, 16 bits wide
  assign xor_1_out = A ^ B;  // XOR_Gate xor_1, 16 bits wide
  Multiplexer #(.select(4), .width(16)) multiplexer_1 (
    .in0(adder_1_out), .in1(and_1_out), .in2(or_1_out), .in3(xor_1_out), .in4(divider_1_out),
    .in5(multiplier_1_out), .in6(subtractor_1_out), .in7(shifter_1_out), .in8(shifter_2_out),
    .in9(shifter_3_out), .in10(shifter_4_out), .in11(negator_1_out), .in12(negator_2_out), .out(Auresult),
    .sel(AUsel));  // open: in13, in14, in15
endmodule

module project_ro (
  input  [15:0] A,
  input  [15:0] B,
  input  [2:0] in_3,
  output RUresult
);

  wire comparator_1_eq, comparator_1_gt, comparator_1_lt, not_1_out, or_1_out, or_2_out;

  Comparator #(.width(16)) comparator_1 (
    .a(A), .b(B), .gt(comparator_1_gt), .eq(comparator_1_eq), .lt(comparator_1_lt));
  or or_1 (or_1_out, comparator_1_gt, comparator_1_eq);
  not not_1 (not_1_out, comparator_1_eq);
  or or_2 (or_2_out, comparator_1_eq, comparator_1_lt);
  Multiplexer #(.select(3)) multiplexer_1 (
    .in0(not_1_out), .in1(comparator_1_eq), .in2(comparator_1_lt), .in3(or_2_out), .in4(comparator_1_gt),
    .in5(or_1_out), .out(RUresult), .sel(in_3));  // open: in6, in7
endmodule

module project_alu (
  input  [3:0] AUsel,
  input  [15:0] A,
  input  [15:0] B,
  input  AU_OE,
  input  [2:0] RUsel,
  output [15:0] Auresult,
  output [15:0] AUDout,
  output RUresult
);

  project_ao project_ao_1 (.AUsel(AUsel), .A(A), .B(B), .Auresult(Auresult));
  project_ro project_ro_1 (.A(A), .B(B), .in_3(RUsel), .RUresult(RUresult));
  assign AUDout = AU_OE ? Auresult : 16'bz;  // Controlled_Buffer controlled_buffer_1
endmodule

module register8bit (
  input  [7:0] Data,
  input  WE,
  input  Clk,
  input  Reset,
  output [7:0] Result
);

  Register register_1 (.D(Data), .en(WE), .clk(Clk), .Q(Result), .clr(Reset));
endmodule

module CPU (
  input  [15:0] Test,
  input  OE,
  input  [3:0] AUSel,
  input  [2:0] RUSel,
  output [15:0] out_5,
  output RUResult
);

  wire clock_1_out, clock_2_out, cu_1_c0, cu_1_c1, cu_1_c2, cu_1_c3, cu_1_c4, cu_1_c5, cu_1_c6, cu_1_c7,
       cu_1_c8, cu_1_c9, cu_1_c10, cu_1_c11, cu_1_c12, cu_1_c13, cu_1_c14, cu_1_c15;
  wire [2:0] StepCounter_q, undriven;
  wire [3:0] bitselector_1_out, decimaldecoder_1_output_32bit, decimaldecoder_1_output_32bit_2,
       decimaldecoder_1_output_32bit_3, decimaldecoder_1_output_32bit_4, decimaldecoder_1_output_32bit_5,
       decimaldecoder_1_output_32bit_6, decimaldecoder_1_output_32bit_7, decimaldecoder_1_output_32bit_8,
       decimaldecoder_2_output_32bit, decimaldecoder_2_output_32bit_2, decimaldecoder_2_output_32bit_3,
       decimaldecoder_2_output_32bit_4, decimaldecoder_2_output_32bit_5, decimaldecoder_2_output_32bit_6,
       decimaldecoder_2_output_32bit_7, decimaldecoder_2_output_32bit_8, decimaldecoder_3_output_32bit,
       decimaldecoder_3_output_32bit_2, decimaldecoder_3_output_32bit_3, decimaldecoder_3_output_32bit_4,
       decimaldecoder_3_output_32bit_5, decimaldecoder_3_output_32bit_6, decimaldecoder_3_output_32bit_7,
       decimaldecoder_3_output_32bit_8, decimaldecoder_4_output_32bit, decimaldecoder_4_output_32bit_2,
       decimaldecoder_4_output_32bit_3, decimaldecoder_4_output_32bit_4, decimaldecoder_4_output_32bit_5,
       decimaldecoder_4_output_32bit_6, decimaldecoder_4_output_32bit_7, decimaldecoder_4_output_32bit_8,
       decimaldecoder_5_output_32bit, decimaldecoder_5_output_32bit_2, decimaldecoder_5_output_32bit_3,
       decimaldecoder_5_output_32bit_4, decimaldecoder_5_output_32bit_5, decimaldecoder_5_output_32bit_6,
       decimaldecoder_5_output_32bit_7, decimaldecoder_5_output_32bit_8, ProgramCounter_q;
  wire [7:0] address_reg_1_output8bit, bitselector_2_out;
  wire [7:4] bitselector_1_out_2;
  wire [15:0] bit_extender_1_out, bit_extender_2_out, controlled_buffer_1_out, instruction_reg_1_result,
       mbr_1_result, project_alu_1_audout, ram_1_dout, reg_a_1_result, reg_b_1_result;

  Clock clock_1 (.out(clock_1_out));
  _7_Segment_Display u_7_segment_display_1 (
    .g(decimaldecoder_1_output_32bit_4[3]), .f(decimaldecoder_1_output_32bit_4[2]),
    .a(decimaldecoder_1_output_32bit_4[1]), .b(decimaldecoder_1_output_32bit_4[0]),
    .e(decimaldecoder_1_output_32bit_8[3]), .d(decimaldecoder_1_output_32bit_8[2]),
    .c(decimaldecoder_1_output_32bit_8[1]), .dp(decimaldecoder_1_output_32bit_8[0]));
  _7_Segment_Display u_7_segment_display_2 (
    .g(decimaldecoder_1_output_32bit_3[3]), .f(decimaldecoder_1_output_32bit_3[2]),
    .a(decimaldecoder_1_output_32bit_3[1]), .b(decimaldecoder_1_output_32bit_3[0]),
    .e(decimaldecoder_1_output_32bit_7[3]), .d(decimaldecoder_1_output_32bit_7[2]),
    .c(decimaldecoder_1_output_32bit_7[1]), .dp(decimaldecoder_1_output_32bit_7[0]));
  _7_Segment_Display u_7_segment_display_3 (
    .g(decimaldecoder_1_output_32bit_2[3]), .f(decimaldecoder_1_output_32bit_2[2]),
    .a(decimaldecoder_1_output_32bit_2[1]), .b(decimaldecoder_1_output_32bit_2[0]),
    .e(decimaldecoder_1_output_32bit_6[3]), .d(decimaldecoder_1_output_32bit_6[2]),
    .c(decimaldecoder_1_output_32bit_6[1]), .dp(decimaldecoder_1_output_32bit_6[0]));
  _7_Segment_Display u_7_segment_display_4 (
    .g(decimaldecoder_1_output_32bit[3]), .f(decimaldecoder_1_output_32bit[2]),
    .a(decimaldecoder_1_output_32bit[1]), .b(decimaldecoder_1_output_32bit[0]),
    .e(decimaldecoder_1_output_32bit_5[3]), .d(decimaldecoder_1_output_32bit_5[2]),
    .c(decimaldecoder_1_output_32bit_5[1]), .dp(decimaldecoder_1_output_32bit_5[0]));
  BitSelector #(.group(8), .width(16)) bitselector_1 (
    .in(controlled_buffer_1_out), .out({bitselector_1_out_2, bitselector_1_out}), .sel(1'b0));
  assign controlled_buffer_1_out = cu_1_c8 ? instruction_reg_1_result : 16'bz;  // Controlled_Buffer controlled_buffer_1
  Instruction_Reg instruction_reg_1 (
    .Clk(clock_1_out), .WE(cu_1_c7), .Data(project_alu_1_audout), .Result(instruction_reg_1_result));  // open: RST
  Reg_A reg_a_1 (
    .Clk(clock_1_out), .WE(cu_1_c12), .Data(project_alu_1_audout), .Result(reg_a_1_result));  // open: RST, OE, Dout
  decimaldecoder decimaldecoder_1 (
    .input_16bit(reg_a_1_result),
    .output_32bit({decimaldecoder_1_output_32bit_8, decimaldecoder_1_output_32bit_7, decimaldecoder_1_output_32bit_6, decimaldecoder_1_output_32bit_5, decimaldecoder_1_output_32bit_4, decimaldecoder_1_output_32bit_3, decimaldecoder_1_output_32bit_2, decimaldecoder_1_output_32bit}));
  project_alu project_alu_1 (
    .A(reg_a_1_result), .B(reg_b_1_result), .RUsel(RUSel), .AUsel(AUSel), .AU_OE(cu_1_c11),
    .RUresult(RUResult), .AUDout(project_alu_1_audout));  // open: Auresult
  LED D15 (.in(project_alu_1_audout[15]));
  _7_Segment_Display u_7_segment_display_5 (
    .g(decimaldecoder_2_output_32bit_4[3]), .f(decimaldecoder_2_output_32bit_4[2]),
    .a(decimaldecoder_2_output_32bit_4[1]), .b(decimaldecoder_2_output_32bit_4[0]),
    .e(decimaldecoder_2_output_32bit_8[3]), .d(decimaldecoder_2_output_32bit_8[2]),
    .c(decimaldecoder_2_output_32bit_8[1]), .dp(decimaldecoder_2_output_32bit_8[0]));
  _7_Segment_Display u_7_segment_display_6 (
    .g(decimaldecoder_2_output_32bit_3[3]), .f(decimaldecoder_2_output_32bit_3[2]),
    .a(decimaldecoder_2_output_32bit_3[1]), .b(decimaldecoder_2_output_32bit_3[0]),
    .e(decimaldecoder_2_output_32bit_7[3]), .d(decimaldecoder_2_output_32bit_7[2]),
    .c(decimaldecoder_2_output_32bit_7[1]), .dp(decimaldecoder_2_output_32bit_7[0]));
  Counter #(.max('h3), .width(4)) ProgramCounter (
    .count(cu_1_c1), .clk(clock_1_out), .D(bitselector_1_out), .Q(ProgramCounter_q));  // open: clr, load, up, carry
  Reg_B reg_b_1 (
    .Clk(clock_1_out), .WE(cu_1_c13), .Data({project_alu_1_audout[15:3], undriven}), .Result(reg_b_1_result));  // open: RST
  LED D14 (.in(project_alu_1_audout[14]));
  LED D12 (.in(project_alu_1_audout[12]));
  LED D13 (.in(project_alu_1_audout[13]));
  _7_Segment_Display u_7_segment_display_7 (
    .g(decimaldecoder_2_output_32bit_2[3]), .f(decimaldecoder_2_output_32bit_2[2]),
    .a(decimaldecoder_2_output_32bit_2[1]), .b(decimaldecoder_2_output_32bit_2[0]),
    .e(decimaldecoder_2_output_32bit_6[3]), .d(decimaldecoder_2_output_32bit_6[2]),
    .c(decimaldecoder_2_output_32bit_6[1]), .dp(decimaldecoder_2_output_32bit_6[0]));
  assign project_alu_1_audout = OE ? Test : 16'bz;  // Controlled_Buffer controlled_buffer_2
  LED D10 (.in(project_alu_1_audout[10]));
  LED D11 (.in(project_alu_1_audout[11]));
  decimaldecoder decimaldecoder_2 (
    .input_16bit(reg_b_1_result),
    .output_32bit({decimaldecoder_2_output_32bit_8, decimaldecoder_2_output_32bit_7, decimaldecoder_2_output_32bit_6, decimaldecoder_2_output_32bit_5, decimaldecoder_2_output_32bit_4, decimaldecoder_2_output_32bit_3, decimaldecoder_2_output_32bit_2, decimaldecoder_2_output_32bit}));
  _7_Segment_Display u_7_segment_display_8 (
    .g(decimaldecoder_2_output_32bit[3]), .f(decimaldecoder_2_output_32bit[2]),
    .a(decimaldecoder_2_output_32bit[1]), .b(decimaldecoder_2_output_32bit[0]),
    .e(decimaldecoder_2_output_32bit_5[3]), .d(decimaldecoder_2_output_32bit_5[2]),
    .c(decimaldecoder_2_output_32bit_5[1]), .dp(decimaldecoder_2_output_32bit_5[0]));
  LED D8 (.in(project_alu_1_audout[8]));
  LED D7 (.in(project_alu_1_audout[7]));
  LED D9 (.in(project_alu_1_audout[9]));
  assign bit_extender_1_out = {{12{1'b0}}, ProgramCounter_q};  // Bit_Extender bit_extender_1
  assign bitselector_1_out = cu_1_c0 ? ProgramCounter_q : 4'bz;  // Controlled_Buffer controlled_buffer_3
  LED D6 (.in(project_alu_1_audout[6]));
  LED D5 (.in(project_alu_1_audout[5]));
  LED D4 (.in(project_alu_1_audout[4]));
  LED D3 (.in(project_alu_1_audout[3]));
  LED D2 (.in(project_alu_1_audout[2]));
  assign project_alu_1_audout = cu_1_c5 ? mbr_1_result : 16'bz;  // Controlled_Buffer controlled_buffer_4
  LED D0 (.in(project_alu_1_audout[0]));
  LED D1 (.in(project_alu_1_audout[1]));
  _7_Segment_Display u_7_segment_display_9 (
    .g(decimaldecoder_3_output_32bit[3]), .f(decimaldecoder_3_output_32bit[2]),
    .a(decimaldecoder_3_output_32bit[1]), .b(decimaldecoder_3_output_32bit[0]),
    .e(decimaldecoder_3_output_32bit_5[3]), .d(decimaldecoder_3_output_32bit_5[2]),
    .c(decimaldecoder_3_output_32bit_5[1]), .dp(decimaldecoder_3_output_32bit_5[0]));
  _7_Segment_Display u_7_segment_display_10 (
    .g(decimaldecoder_4_output_32bit_4[3]), .f(decimaldecoder_4_output_32bit_4[2]),
    .a(decimaldecoder_4_output_32bit_4[1]), .b(decimaldecoder_4_output_32bit_4[0]),
    .e(decimaldecoder_4_output_32bit_8[3]), .d(decimaldecoder_4_output_32bit_8[2]),
    .c(decimaldecoder_4_output_32bit_8[1]), .dp(decimaldecoder_4_output_32bit_8[0]));
  decimaldecoder decimaldecoder_3 (
    .input_16bit(bit_extender_1_out),
    .output_32bit({decimaldecoder_3_output_32bit_8, decimaldecoder_3_output_32bit_7, decimaldecoder_3_output_32bit_6, decimaldecoder_3_output_32bit_5, decimaldecoder_3_output_32bit_4, decimaldecoder_3_output_32bit_3, decimaldecoder_3_output_32bit_2, decimaldecoder_3_output_32bit}));
  assign project_alu_1_audout = cu_1_c14 ? out_5 : 16'bz;  // Controlled_Buffer controlled_buffer_5
  _7_Segment_Display u_7_segment_display_11 (
    .g(decimaldecoder_4_output_32bit_3[3]), .f(decimaldecoder_4_output_32bit_3[2]),
    .a(decimaldecoder_4_output_32bit_3[1]), .b(decimaldecoder_4_output_32bit_3[0]),
    .e(decimaldecoder_4_output_32bit_7[3]), .d(decimaldecoder_4_output_32bit_7[2]),
    .c(decimaldecoder_4_output_32bit_7[1]), .dp(decimaldecoder_4_output_32bit_7[0]));
  assign project_alu_1_audout = cu_1_c6 ? mbr_1_result : 16'bz;  // Controlled_Buffer controlled_buffer_6
  MBR mbr_1 (.Clk(clock_2_out), .WE(cu_1_c4), .Data(project_alu_1_audout), .Result(mbr_1_result));  // open: RST
  Output_Reg output_reg_1 (
    .Clk(clock_2_out), .WE(cu_1_c15), .Data(project_alu_1_audout), .Result(out_5));  // open: RST, OE, Dout
  _7_Segment_Display u_7_segment_display_12 (
    .g(decimaldecoder_4_output_32bit_2[3]), .f(decimaldecoder_4_output_32bit_2[2]),
    .a(decimaldecoder_4_output_32bit_2[1]), .b(decimaldecoder_4_output_32bit_2[0]),
    .e(decimaldecoder_4_output_32bit_6[3]), .d(decimaldecoder_4_output_32bit_6[2]),
    .c(decimaldecoder_4_output_32bit_6[1]), .dp(decimaldecoder_4_output_32bit_6[0]));
  address_reg address_reg_1 (
    .A({bitselector_1_out_2, bitselector_1_out}), .WE(cu_1_c9), .OE(cu_1_c10), .CLK(clock_2_out),
    .output8bit(address_reg_1_output8bit));  // open: reg_8bit_output
  _7_Segment_Display u_7_segment_display_13 (
    .g(decimaldecoder_4_output_32bit[3]), .f(decimaldecoder_4_output_32bit[2]),
    .a(decimaldecoder_4_output_32bit[1]), .b(decimaldecoder_4_output_32bit[0]),
    .e(decimaldecoder_4_output_32bit_5[3]), .d(decimaldecoder_4_output_32bit_5[2]),
    .c(decimaldecoder_4_output_32bit_5[1]), .dp(decimaldecoder_4_output_32bit_5[0]));
  Clock clock_2 (.out(clock_2_out));
  decimaldecoder decimaldecoder_4 (
    .input_16bit(out_5),
    .output_32bit({decimaldecoder_4_output_32bit_8, decimaldecoder_4_output_32bit_7, decimaldecoder_4_output_32bit_6, decimaldecoder_4_output_32bit_5, decimaldecoder_4_output_32bit_4, decimaldecoder_4_output_32bit_3, decimaldecoder_4_output_32bit_2, decimaldecoder_4_output_32bit}));
  assign project_alu_1_audout = cu_1_c3 ? ram_1_dout : 16'bz;  // Controlled_Buffer controlled_buffer_7
  LED P7 (.in(address_reg_1_output8bit[7]));
  LED A15 (.in(project_alu_1_audout[15]));
  LED A14 (.in(project_alu_1_audout[14]));
  LED P6 (.in(address_reg_1_output8bit[6]));
  LED P5 (.in(address_reg_1_output8bit[5]));
  LED A13 (.in(project_alu_1_audout[13]));
  LED A11 (.in(project_alu_1_audout[11]));
  LED A12 (.in(project_alu_1_audout[12]));
  Counter #(.max('h5), .width(3)) StepCounter (
    .clk(clock_1_out), .Q(StepCounter_q));  // open: clr, load, up, count, D, carry
  LED P4 (.in(address_reg_1_output8bit[4]));
  LED P3 (.in(address_reg_1_output8bit[3]));
  LED P2 (.in(address_reg_1_output8bit[2]));
  LED A9 (.in(project_alu_1_audout[9]));
  LED A10 (.in(project_alu_1_audout[10]));
  LED P1 (.in(address_reg_1_output8bit[1]));
  LED P0 (.in(address_reg_1_output8bit[0]));
  LED A7 (.in(project_alu_1_audout[7]));
  LED A6 (.in(project_alu_1_audout[6]));
  LED A8 (.in(project_alu_1_audout[8]));
  BitSelector #(.group(8), .width(16)) bitselector_2 (
    .in(instruction_reg_1_result), .out(bitselector_2_out), .sel(1'b1));
  LED A3 (.in(project_alu_1_audout[3]));
  LED A5 (.in(project_alu_1_audout[5]));
  LED A4 (.in(project_alu_1_audout[4]));
  LED A1 (.in(project_alu_1_audout[1]));
  LED A2 (.in(project_alu_1_audout[2]));
  RAM #(.dataWidth(16), .enables("line"), .\type ("nonvolatile")) ram_1 (
    .addr(address_reg_1_output8bit), .we(cu_1_c2), .clk(clock_2_out), .din(project_alu_1_audout),
    .dout(ram_1_dout));
  LED A0 (.in(project_alu_1_audout[0]));
  assign bit_extender_2_out = {{13{1'b0}}, StepCounter_q};  // Bit_Extender bit_extender_2
  _7_Segment_Display u_7_segment_display_14 (
    .g(decimaldecoder_5_output_32bit_4[3]), .f(decimaldecoder_5_output_32bit_4[2]),
    .a(decimaldecoder_5_output_32bit_4[1]), .b(decimaldecoder_5_output_32bit_4[0]),
    .e(decimaldecoder_5_output_32bit_8[3]), .d(decimaldecoder_5_output_32bit_8[2]),
    .c(decimaldecoder_5_output_32bit_8[1]), .dp(decimaldecoder_5_output_32bit_8[0]));
  _7_Segment_Display u_7_segment_display_15 (
    .g(decimaldecoder_5_output_32bit_3[3]), .f(decimaldecoder_5_output_32bit_3[2]),
    .a(decimaldecoder_5_output_32bit_3[1]), .b(decimaldecoder_5_output_32bit_3[0]),
    .e(decimaldecoder_5_output_32bit_7[3]), .d(decimaldecoder_5_output_32bit_7[2]),
    .c(decimaldecoder_5_output_32bit_7[1]), .dp(decimaldecoder_5_output_32bit_7[0]));
  _7_Segment_Display u_7_segment_display_16 (
    .g(decimaldecoder_5_output_32bit_2[3]), .f(decimaldecoder_5_output_32bit_2[2]),
    .a(decimaldecoder_5_output_32bit_2[1]), .b(decimaldecoder_5_output_32bit_2[0]),
    .e(decimaldecoder_5_output_32bit_6[3]), .d(decimaldecoder_5_output_32bit_6[2]),
    .c(decimaldecoder_5_output_32bit_6[1]), .dp(decimaldecoder_5_output_32bit_6[0]));
  _7_Segment_Display u_7_segment_display_17 (
    .g(decimaldecoder_5_output_32bit[3]), .f(decimaldecoder_5_output_32bit[2]),
    .a(decimaldecoder_5_output_32bit[1]), .b(decimaldecoder_5_output_32bit[0]),
    .e(decimaldecoder_5_output_32bit_5[3]), .d(decimaldecoder_5_output_32bit_5[2]),
    .c(decimaldecoder_5_output_32bit_5[1]), .dp(decimaldecoder_5_output_32bit_5[0]));
  CU cu_1 (
    .OPC7(bitselector_2_out[7]), .OPC6(bitselector_2_out[6]), .OPC5(bitselector_2_out[5]),
    .OPC4(bitselector_2_out[4]), .OPC3(bitselector_2_out[3]), .OPC2(bitselector_2_out[2]),
    .OPC1(bitselector_2_out[1]), .OPC0(bitselector_2_out[0]), .SC2(StepCounter_q[2]), .SC1(StepCounter_q[1]),
    .SC0(StepCounter_q[0]), .C0(cu_1_c0), .C1(cu_1_c1), .C2(cu_1_c2), .C3(cu_1_c3), .C4(cu_1_c4),
    .C5(cu_1_c5), .C6(cu_1_c6), .C7(cu_1_c7), .C8(cu_1_c8), .C9(cu_1_c9), .C10(cu_1_c10), .C11(cu_1_c11),
    .C12(cu_1_c12), .C13(cu_1_c13), .C14(cu_1_c14), .C15(cu_1_c15));
  decimaldecoder decimaldecoder_5 (
    .input_16bit(bit_extender_2_out),
    .output_32bit({decimaldecoder_5_output_32bit_8, decimaldecoder_5_output_32bit_7, decimaldecoder_5_output_32bit_6, decimaldecoder_5_output_32bit_5, decimaldecoder_5_output_32bit_4, decimaldecoder_5_output_32bit_3, decimaldecoder_5_output_32bit_2, decimaldecoder_5_output_32bit}));

  // Notes on the sheet:
  //   Internal Address Bus
  //   Internal Data Bus
  //   External Address Bus
  //   External Data Bus
endmodule

module decimaldecoder (
  input  [15:0] input_16bit,
  output [31:0] output_32bit
);

  ROM #(.addrWidth(16), .dataWidth(32)) rom_1 (
    .addr(input_16bit),
    .data({output_32bit[31:28], output_32bit[15:12], output_32bit[27:24], output_32bit[11:8], output_32bit[23:20], output_32bit[7:4], output_32bit[19:16], output_32bit[3:0]}));

  // Notes on the sheet:
  //   contents of rom_1 (hex, n*v repeats v):
  //   e7 21 cb 6b 2d 6e ee 23 ef 2f 21e7 2121 21cb 216b 212d 216e 21ee 2123 21ef 212f cbe7 cb21 cbcb cb6b
  //   cb2d cb6e cbee cb23 cbef cb2f 6be7 6b21 6bcb 6b6b 6b2d 6b6e 6bee 6b23 6bef 6b2f 2de7 2d21 2dcb 2d6b
  //   2d2d 2d6e 2dee 2d23 2def 2d2f 6ee7 6e21 6ecb 6e6b 6e2d 6e6e 6eee 6e23 6eef 6e2f eee7 ee21 eecb ee6b
  //   ee2d ee6e eeee ee23 eeef ee2f 23e7 2321 23cb 236b 232d 236e 23ee 2323 23ef 232f efe7 ef21 efcb ef6b
  //   ef2d ef6e efee ef23 efef ef2f 2fe7 2f21 2fcb 2f6b 2f2d 2f6e 2fee 2f23 2fef 2f2f 21e7e7 21e721 21e7cb
  //   21e76b 21e72d 21e76e 21e7ee 21e723 21e7ef 21e72f 2121e7 212121 2121cb 21216b 21212d 21216e 2121ee
  //   212123 2121ef 21212f 21cbe7 21cb21 21cbcb 21cb6b 21cb2d 21cb6e 21cbee 21cb23 21cbef 21cb2f 216be7
  //   216b21 216bcb 216b6b 216b2d 216b6e 216bee 216b23 216bef 216b2f 212de7 212d21 212dcb 212d6b 212d2d
  //   212d6e 212dee 212d23 212def 212d2f 216ee7 216e21 216ecb 216e6b 216e2d 216e6e 216eee 216e23 216eef
  //   216e2f 21eee7 21ee21 21eecb 21ee6b 21ee2d 21ee6e 21eeee 21ee23 21eeef 21ee2f 2123e7 212321 2123cb
  //   21236b 21232d 21236e 2123ee 212323 2123ef 21232f 21efe7 21ef21 21efcb 21ef6b 21ef2d 21ef6e 21efee
  //   21ef23 21efef 21ef2f 212fe7 212f21 212fcb 212f6b 212f2d 212f6e 212fee 212f23 212fef 212f2f cbe7e7
  //   cbe721 cbe7cb cbe76b cbe72d cbe76e cbe7ee cbe723 cbe7ef cbe72f cb21e7 cb2121 cb21cb cb216b cb212d
  //   cb216e cb21ee cb2123 cb21ef cb212f cbcbe7 cbcb21 cbcbcb cbcb6b cbcb2d cbcb6e cbcbee cbcb23 cbcbef
  //   cbcb2f cb6be7 cb6b21 cb6bcb cb6b6b cb6b2d cb6b6e cb6bee cb6b23 cb6bef cb6b2f cb2de7 cb2d21 cb2dcb
  //   cb2d6b cb2d2d cb2d6e cb2dee cb2d23 cb2def cb2d2f cb6ee7 cb6e21 cb6ecb cb6e6b cb6e2d cb6e6e
endmodule

module CU (
  input  OPC7,
  input  OPC6,
  input  OPC5,
  input  OPC4,
  input  OPC3,
  input  OPC2,
  input  OPC1,
  input  OPC0,
  input  SC2,
  input  SC1,
  input  SC0,
  output C0,
  output C1,
  output C2,
  output C3,
  output C4,
  output C5,
  output C6,
  output C7,
  output C8,
  output C9,
  output C10,
  output C11,
  output C12,
  output C13,
  output C14,
  output C15
);

  wire and_4_out, and_5_out, and_6_out, and_7_out, and_8_out, and_9_out, and_10_out, and_13_out, and_14_out,
       and_15_out, and_16_out, and_17_out, and_18_out, and_19_out, and_20_out, not_1_out, not_2_out,
       not_3_out, not_4_out, not_5_out;

  not not_1 (not_1_out, OPC1);
  not not_2 (not_2_out, OPC0);
  not not_3 (not_3_out, SC2);
  not not_4 (not_4_out, SC1);
  not not_5 (not_5_out, SC0);
  and and_1 (C0, not_3_out, not_4_out, not_5_out);
  and and_2 (C1, not_3_out, not_4_out, SC0);
  and and_3 (C2, OPC1, OPC0, SC2, not_4_out, not_5_out);
  and and_4 (and_4_out, not_3_out, not_4_out, SC0);
  and and_5 (and_5_out, not_1_out, SC2, not_4_out, not_5_out);
  and and_6 (and_6_out, not_3_out, not_4_out, SC0);
  and and_7 (and_7_out, not_1_out, SC2, not_4_out, not_5_out);
  and and_8 (and_8_out, OPC1, OPC0, not_3_out, SC0);
  and and_9 (and_9_out, not_3_out, SC1, not_5_out);
  and and_10 (and_10_out, not_1_out, SC2, not_4_out, SC0);
  and and_11 (C6, OPC1, OPC0, SC2, not_4_out, not_5_out);
  and and_12 (C7, not_3_out, SC1, not_5_out);
  and and_13 (and_13_out, not_1_out, not_3_out, SC1, SC0);
  and and_14 (and_14_out, OPC0, not_3_out, SC1, SC0);
  and and_15 (and_15_out, not_3_out, not_4_out, not_5_out);
  and and_16 (and_16_out, not_1_out, not_3_out, SC1, SC0);
  and and_17 (and_17_out, OPC0, not_3_out, SC1, SC0);
  and and_18 (and_18_out, not_3_out, not_4_out, SC0);
  and and_19 (and_19_out, not_1_out, SC2, not_4_out, not_5_out);
  and and_20 (and_20_out, OPC0, SC2, not_4_out, not_5_out);
  and and_21 (C11, OPC1, not_2_out, not_3_out, SC1, SC0);
  and and_22 (C12, not_1_out, not_2_out, SC2, not_4_out, SC0);
  and and_23 (C13, not_1_out, OPC0, SC2, not_4_out, SC0);
  and and_24 (C14, OPC1, OPC0, not_3_out, SC1, SC0);
  and and_25 (C15, OPC1, not_2_out, not_3_out, SC1, SC0);
  or or_1 (C3, and_4_out, and_5_out);
  or or_2 (C4, and_6_out, and_7_out, and_8_out);
  or or_3 (C5, and_9_out, and_10_out);
  or or_4 (C8, and_13_out, and_14_out);
  or or_5 (C9, and_15_out, and_16_out, and_17_out);
  or or_6 (C10, and_18_out, and_19_out, and_20_out);
endmodule

module Instruction_Reg (
  input  [15:0] Data,
  input  WE,
  input  Clk,
  input  RST,
  output [15:0] Result
);

  Register #(.width(16)) register_1 (.D(Data), .en(WE), .clk(Clk), .Q(Result), .clr(RST));
endmodule

module Output_Reg (
  input  [15:0] Data,
  input  WE,
  input  Clk,
  input  OE,
  input  RST,
  output [15:0] Result,
  output [15:0] Dout
);

  Register #(.width(16)) register_1 (.D(Data), .en(WE), .clk(Clk), .Q(Result), .clr(RST));
  assign Dout = OE ? Result : 16'bz;  // Controlled_Buffer controlled_buffer_1
endmodule

module Reg_A (
  input  [15:0] Data,
  input  WE,
  input  Clk,
  input  OE,
  input  RST,
  output [15:0] Result,
  output [15:0] Dout
);

  Register #(.width(16)) register_1 (.D(Data), .en(WE), .clk(Clk), .Q(Result), .clr(RST));
  assign Dout = OE ? Result : 16'bz;  // Controlled_Buffer controlled_buffer_1
endmodule

module Reg_B (
  input  [15:0] Data,
  input  WE,
  input  Clk,
  input  RST,
  output [15:0] Result
);

  Register #(.width(16)) register_1 (.D(Data), .en(WE), .clk(Clk), .Q(Result), .clr(RST));
endmodule

module MAR (
  input  [7:0] in_1,
  input  in_2,
  input  in_3,
  input  in_4,
  input  in_5,
  output [7:0] out_6,
  output [7:0] out_7
);

  // memory1bit memory1bit_1: pin names not known; wires that end beside it: in_2, in_5, in_1[7], in_3, in_4, out_7[7], out_6[7]
  // memory1bit memory1bit_2: pin names not known; wires that end beside it: in_2, in_5, in_1[6], in_3, in_4, out_7[6], out_6[6]
  // memory1bit memory1bit_3: pin names not known; wires that end beside it: in_2, in_5, in_1[5], in_3, in_4, out_7[5], out_6[5]
  // memory1bit memory1bit_4: pin names not known; wires that end beside it: in_2, in_5, in_1[4], in_3, in_4, out_7[4], out_6[4]
  // memory1bit memory1bit_5: pin names not known; wires that end beside it: in_2, in_5, in_1[3], in_3, in_4, out_7[3], out_6[3]
  // memory1bit memory1bit_6: pin names not known; wires that end beside it: in_2, in_5, in_1[2], in_3, in_4, out_7[2], out_6[2]
  // memory1bit memory1bit_7: pin names not known; wires that end beside it: in_2, in_5, in_1[1], in_3, in_4, out_7[1], out_6[1]
  // memory1bit memory1bit_8: pin names not known; wires that end beside it: in_2, in_5, in_1[0], in_3, in_4, out_7[0], out_6[0]

  // Notes on the sheet:
  //   WE
  //   Reset
  //   Clk
  //   OE
  //   Din
  //   Stored Data
  //   Dout
endmodule

module MBR (
  input  [15:0] Data,
  input  WE,
  input  Clk,
  input  RST,
  output [15:0] Result
);

  Register #(.width(16)) register_1 (.D(Data), .en(WE), .clk(Clk), .Q(Result), .clr(RST));
endmodule

module memory1bit (
  input  in_1,
  input  Din,
  input  Reset,
  input  in_4,
  input  in_5,
  output out_6,
  output out_7
);

  wire and_1_out, and_2_out, not_1_out, or_1_out;

  not not_1 (not_1_out, in_1);
  and and_1 (and_1_out, out_7, not_1_out);
  and and_2 (and_2_out, in_1, Din);
  or or_1 (or_1_out, and_1_out, and_2_out);
  D_Flip_Flop d_ff_1 (.D(or_1_out), .clk(in_5), .Q(out_7), .reset(Reset));  // open: Qn, preset
  assign out_6 = in_4 ? out_7 : 1'bz;  // Controlled_Buffer controlled_buffer_1

  // Notes on the sheet:
  //   WE
  //   OE
  //   clk
  //   ctrled buffer
  //   Dout
  //   stored data
endmodule

module address_reg (
  input  [7:0] A,
  input  WE,
  input  OE,
  input  CLK,
  output [7:0] output8bit,
  output [7:0] reg_8bit_output
);

  MAR mar_1 (.in_2(WE), .in_4(CLK), .in_5(OE), .in_1(A), .out_6(output8bit), .out_7(reg_8bit_output));  // open: in_3
endmodule
