// Logisim project project_alu.circ as structural Verilog: 3 circuits, main circuit project_ao
module project_ao (
  input  [3:0] AUsel,
  input  [15:0] A,
  input  [15:0] B,
  output [15:0] Auresult
);

  wire [15:0] adder_1_out, and_1_out, divider_1_out, multiplier_1_out, negator_1_out, negator_2_out,
       or_1_out, shifter_1_out, shifter_2_out, shifter_3_out, shifter_4_out, subtractor_1_out, xor_1_out;

  Adder #(.width(16)) adder_1 (.a(A), .b(B), .out(adder_1_out));  // open: cin, cout
  Divider #(.width(16)) divider_1 (.a(A), .b(B), .out(divider_1_out));  // open: upper, rem
  Multiplier #(.width(16)) multiplier_1 (.a(A), .b(B), .out(multiplier_1_out));  // open: cin, cout
  Subtractor #(.width(16)) subtractor_1 (.a(A), .b(B), .out(subtractor_1_out));  // open: bin, bout
  Shifter #(.width(16)) shifter_1 (.in(A), .\dist (4'b0010), .out(shifter_1_out));
  Shifter #(.width(16)) shifter_2 (.in(B), .\dist (4'b0010), .out(shifter_2_out));
  Shifter #(.shift("lr"), .width(16)) shifter_3 (.in(A), .\dist (4'b0010), .out(shifter_3_out));
  Shifter #(.shift("lr"), .width(16)) shifter_4 (.in(B), .\dist (4'b0010), .out(shifter_4_out));
  Negator #(.width(16)) negator_1 (.in(A), .out(negator_1_out));
  Negator #(.width(16)) negator_2 (.in(B), .out(negator_2_out));
  assign and_1_out = A & B;  // AND_Gate and_1, 16 bits wide
  assign or_1_out = A | B;  // OR_Gate or_1, 16 bits wide
  assign xor_1_out = A ^ B;  // XOR_Gate xor_1, 16 bits wide
  Multiplexer #(.select(4), .width(16)) multiplexer_1 (
    .in0(adder_1_out), .in1(and_1_out), .in2(or_1_out), .in3(xor_1_out), .in4(divider_1_out),
    .in5(multiplier_1_out), .in6(subtractor_1_out), .in7(shifter_1_out), .in8(shifter_2_out),
    .in9(shifter_3_out), .in10(shifter_4_out), .in11(negator_1_out), .in12(negator_2_out), .out(Auresult),
    .sel(AUsel));  // open: in13, in14, in15
endmodule

module project_ro (
  input  [15:0] A,
  input  [15:0] B,
  input  [2:0] in_3,
  output RUresult
);

  wire comparator_1_eq, comparator_1_gt, comparator_1_lt, not_1_out, or_1_out, or_2_out;

  Comparator #(.width(16)) comparator_1 (
    .a(A), .b(B), .gt(comparator_1_gt), .eq(comparator_1_eq), .lt(comparator_1_lt));
  or or_1 (or_1_out, comparator_1_gt, comparator_1_eq);
  not not_1 (not_1_out, comparator_1_eq);
  or or_2 (or_2_out, comparator_1_eq, comparator_1_lt);
  Multiplexer #(.select(3)) multiplexer_1 (
    .in0(not_1_out), .in1(comparator_1_eq), .in2(comparator_1_lt), .in3(or_2_out), .in4(comparator_1_gt),
    .in5(or_1_out), .out(RUresult), .sel(in_3));  // open: in6, in7
endmodule

module project_alu (
  input  [3:0] in_1,
  input  [15:0] in_2,
  input  [15:0] in_3,
  input  [2:0] in_4,
  output [15:0] out_5,
  output [15:0] out_6,
  output out_7
);

  project_ao project_ao_1 (.AUsel(in_1), .A(in_2), .B(in_3), .Auresult(out_5));
  project_ro project_ro_1 (.A(in_2), .B(in_3), .in_3(in_4), .RUresult(out_7));
  assign out_6 = ~out_5;  // NOT_Gate not_1, 16 bits wide
endmodule
